# Fritzing sketch sketch (saved by Fritzing 0.9.3b)

parts:
  Part1 = Arduino Pro Mini (3.3V) [part_number="Pro Mini 3.3V"]
  U1 = LIPO-2000mAh [package=lipo-2000]
  Part2 = Real Time Clock Module - DS1307 RTC Breakout Board [part_number=DS1307]
  R1 = Rotary Potentiometer (Small) [maximum_resistance=10kΩ part_number="10K Poti" package=THT]
  R2 = Photocell (LDR) [part_number="Photo Resistor" package=THT]
  J1 = single row smd female pin header, 7 pins [form="♀ (female)" part_number="SD Adapter Card"]

nets:
  N1: Part1.GND, U1.-, R1.leg1, J1.pin2, J1.pin5
  N2: Part1.A4, Part2.SDA
  N3: Part1.A5, Part2.SCL
  N4: Part1.RAW, U1.+
  VCC: Part1.VCC, Part2.5V, R2.pin_1, J1.pin4
  N5: Part1.SCK, J1.pin3
  N6: Part1.MISO, J1.pin1
  N7: Part1.MOSI, J1.pin6
  N8: Part1.D10, J1.pin7
  N9: Part1.D9, Part2.GND
  N10: Part1.D2, R1.wiper
  N11: R1.leg2, R2.pin_0
